# Fritzing sketch relay (saved by Fritzing 0.9.3b)
breadboards: 1

parts:
  Part1 = Arduino Uno (Rev3)
  YwRobot_Power_Supply1 = YwRobot Breadboard Power Supply [part_number=545043]
  M1 = DC Motor
  KY-1 = Keyes Relay [package=THT]

nets:
  N1: Part1.D6_PWM, KY-1.signal
  N2: Part1.5V, KY-1.power
  N3: Part1.GND, KY-1.ground
  N4: YwRobot_Power_Supply1.VCC#5, KY-1.C
  N5: YwRobot_Power_Supply1.GND#11, M1.pin_2
  N6: M1.pin_1, KY-1.NO

custom parts:
  YwRobot Breadboard Power Supply: The YwRobot Breadboard Power Supply (MB-V2) has two power rails; they can be 5V or 3V3. Power to the module can be provided through the female USB socket or through the A10 (female) 2.1mm power jack.
  Keyes Relay: The Keyes 5V relay module is suitable for SCM development, home appliance control. It uses a 5V~12V TIL control signal which can control DC / AC signal.
