# Fritzing sketch Stepper (saved by Fritzing 0.9.3b)

parts:
  X = Stepper Motor - Bipolar
  Part2 = Arduino Uno (Rev3)
  12V = 2.1mm Barrel Jack with Terminal Block
  MD09B1 = A4988 Stepper Motor Driver Carrier  # not connected
  MD09B2 = A4988 Stepper Motor Driver Carrier

nets:
  N1: X.A, MD09B2.OUT_2B
  N2: X.C, MD09B2.OUT_2A
  N3: X.B, MD09B2.OUT_1A
  N4: X.D, MD09B2.OUT_1B
  N5: Part2.D8, MD09B2.Enable
  N6: Part2.D2, MD09B2.STEP
  N7: Part2.D3_PWM, MD09B2.DIR
  5V: Part2.5V, MD09B2.VDD
  N8: Part2.GND, MD09B2.GROUND#147
  N9: 12V.POS, MD09B2.VMOT
  N10: 12V.NEG, MD09B2.GROUND#141

notes:
  2B
  2A
  1A
  1B
  ENA
  STP
  DIR
