# Fritzing sketch Stepper_Rotary (saved by Fritzing 0.9.3b)

parts:
  X = Stepper Motor - Bipolar
  Part2 = Arduino Uno (Rev3)
  12V = 2.1mm Barrel Jack with Terminal Block
  MD09B1 = A4988 Stepper Motor Driver Carrier  # not connected
  MD09B2 = A4988 Stepper Motor Driver Carrier
  RE1 = KY-040 Rotary encoder [package=THT]

nets:
  N1: X.A, MD09B2.OUT_2B
  N2: X.C, MD09B2.OUT_2A
  N3: X.B, MD09B2.OUT_1A
  N4: X.D, MD09B2.OUT_1B
  N5: Part2.D8, MD09B2.Enable
  N6: Part2.D2, MD09B2.STEP
  N7: Part2.D3_PWM, MD09B2.DIR
  N8: Part2.D4, RE1.SW
  N9: Part2.D5_PWM, RE1.DT
  N10: Part2.D6_PWM, RE1.CLK
  5V: Part2.5V, MD09B2.VDD, RE1.Vcc
  GND: Part2.GND, MD09B2.GROUND#147, RE1.GND
  N11: 12V.POS, MD09B2.VMOT
  N12: 12V.NEG, MD09B2.GROUND#141

notes:
  2B
  2A
  1A
  1B
  ENA
  STP
  DIR

custom parts:
  KY-040 Rotary encoder: KY-040 Rotary Encoder with switch on breakout borad from AZ Delivery
