# Fritzing sketch 05.01.push_sw_uno (saved by Fritzing 0.9.3b)
breadboards: 1

parts:
  S4 = Momentary Switch [package=ksa_sealed_tac_switch]
  LED1 = LED - 5mm [color="Red (633nm)" package="5 mm [THT]"]
  R1 = Resistor [tolerance=±5% resistance=220 package="0805 [SMD]"]
  Part1 = Arduino Uno (Rev3) - ICSP
  S5 = Momentary Switch [package=ksa_sealed_tac_switch]

nets:
  N1: S4.1, S4.2, LED1.cathode, Part1.GND, S5.1, S5.2
  N2: S4.3, S4.4, Part1.D2
  N3: LED1.anode, R1.Pin_0
  N4: R1.Pin_1, Part1.D5_PWM
  N5: Part1.D3_PWM, S5.3, S5.4
